// Logisim project ex2.circ as structural Verilog: 1 circuit, main circuit compute_BrUn
module compute_BrUn (
  input  [31:0] INSTRUCTION,
  output BrUn
);

  wire and_1_out, comparator_1_eq, comparator_2_eq;

  Comparator #(.width(7)) comparator_1 (.a(7'b1100011), .b(INSTRUCTION[6:0]), .eq(comparator_1_eq));  // open: gt, lt
  Comparator #(.width(1)) comparator_2 (.a(INSTRUCTION[13]), .b(1'b1), .eq(comparator_2_eq));  // open: gt, lt
  and and_1 (and_1_out, comparator_1_eq, comparator_2_eq);
  Multiplexer multiplexer_1 (.in0(1'b0), .in1(1'b1), .out(BrUn), .sel(and_1_out));
endmodule
